// Logisim project cpu.circ as structural Verilog: 10 circuits, main circuit main
module main (
  input  in_1,
  output [31:0] out_2,
  output out_3,
  output [4:0] out_4,
  output [31:0] out_5,
  output out_6,
  output [4:0] out_7,
  output [31:0] out_8
);

  wire ALUSource, Branch, MemtoReg, PCSource, RegDst;
  wire [1:0] EXTControl;
  wire [2:0] ALUControl;
  wire [4:0] ifu_1_rd, ifu_1_rs, ifu_1_rt;
  wire [5:0] ifu_1_out_5, ifu_1_out_9;
  wire [15:0] ifu_1_out_3;
  wire [31:0] alu_1_aluresult, dm_1_readdata, ext_1_immextend, grf_1_rd1, ifu_1_pc, multiplexer_2_out,
       npc_1_npc;

  NPC npc_1 (.in_1(ifu_1_pc), .in_2(ifu_1_out_3), .in_3(PCSource), .NPC(npc_1_npc));
  IFU ifu_1 (
    .in_1(in_1), .in_2(npc_1_npc), .out_3(ifu_1_out_3), .PC(ifu_1_pc), .out_5(ifu_1_out_5), .rd(ifu_1_rd),
    .rt(ifu_1_rt), .rs(ifu_1_rs), .out_9(ifu_1_out_9), .Instr(out_2));
  Multiplexer #(.width(5)) multiplexer_1 (.in0(ifu_1_rt), .in1(ifu_1_rd), .out(out_4), .sel(RegDst));  // open: en
  EXT ext_1 (.in_1(ifu_1_out_3), .in_2(EXTControl), .ImmExtend(ext_1_immextend));
  Controller controller_1 (
    .in_1(ifu_1_out_9), .in_2(ifu_1_out_5), .in_3(out_2), .RegDst(RegDst), .RegWrite(out_3),
    .MemtoReg(MemtoReg), .ALUSource(ALUSource), .MemWrite(out_6), .Branch(Branch), .EXTControl(EXTControl),
    .ALUControl(ALUControl));
  GRF grf_1 (
    .in_1(in_1), .in_2(out_3), .in_3(ifu_1_rs), .RD1(grf_1_rd1), .in_4(ifu_1_rt), .in_5(out_4),
    .out_8(out_8), .in_6(out_5));
  Multiplexer #(.width(32)) multiplexer_2 (
    .in0(out_8), .in1(ext_1_immextend), .out(multiplexer_2_out), .sel(ALUSource));  // open: en
  ALU alu_1 (
    .in_1(ALUControl), .in_2(grf_1_rd1), .in_3(multiplexer_2_out),
    .ALUResult({alu_1_aluresult[31:7], out_7, alu_1_aluresult[1:0]}));
  BranchControl branchcontrol_1 (
    .ALUResult({alu_1_aluresult[31:7], out_7, alu_1_aluresult[1:0]}), .Branch(Branch), .PCSource(PCSource));
  DM dm_1 (
    .in_1(in_1), .in_2(out_6), .in_3({alu_1_aluresult[31:7], out_7, alu_1_aluresult[1:0]}), .in_4(out_8),
    .ReadData(dm_1_readdata));
  Multiplexer #(.width(32)) multiplexer_3 (
    .in0({alu_1_aluresult[31:7], out_7, alu_1_aluresult[1:0]}), .in1(dm_1_readdata), .out(out_5),
    .sel(MemtoReg));  // open: en

  // Other names for the same wires on the sheet: MemAddr[4:0] = out_7; Instr[31:0] = out_2; MemData[31:0] = out_8;
  //   MemWrite = out_6; RegAddr[4:0] = out_4; RegData[31:0] = out_5; RegWrite = out_3; reset = in_1
endmodule

module IFU (
  input  in_1,
  input  [31:0] in_2,
  output [15:0] out_3,
  output [31:0] PC,
  output [5:0] out_5,
  output [4:0] rd,
  output [4:0] rt,
  output [4:0] rs,
  output [5:0] out_9,
  output [31:0] Instr
);

  wire clock_1_out;

  Clock clock_1 (.out(clock_1_out));
  Register #(.width(32)) register_1 (.D(in_2), .Q(PC), .clk(clock_1_out), .clr(in_1));  // open: en
  ROM #(.addrWidth(5), .dataWidth(32)) rom_1 (.addr(PC[6:2]), .data(Instr));  // open: sel

  assign out_3 = Instr[15:0];
  assign out_5 = Instr[5:0];
  assign out_9 = Instr[31:26];
  assign rd = Instr[15:11];
  assign rs = Instr[25:21];
  assign rt = Instr[20:16];

  // Other names for the same wires on the sheet: NPC[31:0] = in_2; reset = in_1

  // Notes on the sheet:
  //   PC
  //   func
  //   Opcode
  //   Imm
endmodule

module GRF (
  input  in_1,
  input  in_2,
  input  [4:0] in_3,
  input  [4:0] in_4,
  input  [4:0] in_5,
  input  [31:0] in_6,
  output [31:0] RD1,
  output [31:0] out_8
);

  wire clk;
  wire [31:0] R0, R1, R2, R3, R4, R5, R6, R7, R8, R9, R10, R11, R12, R13, R14, R15, R16, R17, R18, R19, R20,
       R21, R22, R23, R24, R25, R26, R27, R28, R29, R30, R31, W1, W2, W3, W4, W5, W6, W7, W8, W9, W10, W11,
       W12, W13, W14, W15, W16, W17, W18, W19, W20, W21, W22, W23, W24, W25, W26, W27, W28, W29, W30, W31;

  Register #(.width(32)) register_1 (.D(W14), .en(in_2), .Q(R14), .clk(clk), .clr(in_1));
  Register #(.width(32)) register_2 (.D(W23), .en(in_2), .Q(R23), .clk(clk), .clr(in_1));
  Clock clock_1 (.out(clk));
  Register #(.width(32)) register_3 (.D({32{1'b0}}), .en(in_2), .Q(R0), .clk(clk), .clr(in_1));
  Register #(.width(32)) register_4 (.D(W7), .en(in_2), .Q(R7), .clk(clk), .clr(in_1));
  Multiplexer #(.select(5), .width(32), .enable("false")) multiplexer_1 (
    .in0(R0), .in1(R1), .in2(R2), .in3(R3), .in4(R4), .in5(R5), .in6(R6), .in7(R7), .in8(R8), .in9(R9),
    .in10(R10), .in11(R11), .in12(R12), .in13(R13), .in14(R14), .in15(R15), .in16(R16), .in17(R17),
    .in18(R18), .in19(R19), .in20(R20), .in21(R21), .in22(R22), .in23(R23), .in24(R24), .in25(R25),
    .in26(R26), .in27(R27), .in28(R28), .in29(R29), .in30(R30), .in31(R31), .out(RD1), .sel(in_3));
  Register #(.width(32)) register_5 (.D(W15), .en(in_2), .Q(R15), .clk(clk), .clr(in_1));
  Register #(.width(32)) register_6 (.D(W24), .en(in_2), .Q(R24), .clk(clk), .clr(in_1));
  Register #(.width(32)) register_7 (.D(W1), .en(in_2), .Q(R1), .clk(clk), .clr(in_1));
  Register #(.width(32)) register_8 (.D(W8), .en(in_2), .Q(R8), .clk(clk), .clr(in_1));
  Register #(.width(32)) register_9 (.D(W16), .en(in_2), .Q(R16), .clk(clk), .clr(in_1));
  Register #(.width(32)) register_10 (.D(W25), .en(in_2), .Q(R25), .clk(clk), .clr(in_1));
  Register #(.width(32)) register_11 (.D(W2), .en(in_2), .Q(R2), .clk(clk), .clr(in_1));
  Register #(.width(32)) register_12 (.D(W9), .en(in_2), .Q(R9), .clk(clk), .clr(in_1));
  Register #(.width(32)) register_13 (.D(W17), .en(in_2), .Q(R17), .clk(clk), .clr(in_1));
  Register #(.width(32)) register_14 (.D(W26), .en(in_2), .Q(R26), .clk(clk), .clr(in_1));
  Multiplexer #(.select(5), .width(32), .enable("false")) multiplexer_2 (
    .in0(R0), .in1(R1), .in2(R2), .in3(R3), .in4(R4), .in5(R5), .in6(R6), .in7(R7), .in8(R8), .in9(R9),
    .in10(R10), .in11(R11), .in12(R12), .in13(R13), .in14(R14), .in15(R15), .in16(R16), .in17(R17),
    .in18(R18), .in19(R19), .in20(R20), .in21(R21), .in22(R22), .in23(R23), .in24(R24), .in25(R25),
    .in26(R26), .in27(R27), .in28(R28), .in29(R29), .in30(R30), .in31(R31), .out(out_8), .sel(in_4));
  Register #(.width(32)) register_15 (.D(W3), .en(in_2), .Q(R3), .clk(clk), .clr(in_1));
  Register #(.width(32)) register_16 (.D(W10), .en(in_2), .Q(R10), .clk(clk), .clr(in_1));
  Register #(.width(32)) register_17 (.D(W18), .en(in_2), .Q(R18), .clk(clk), .clr(in_1));
  Register #(.width(32)) register_18 (.D(W27), .en(in_2), .Q(R27), .clk(clk), .clr(in_1));
  Register #(.width(32)) register_19 (.D(W4), .en(in_2), .Q(R4), .clk(clk), .clr(in_1));
  Register #(.width(32)) register_20 (.D(W11), .en(in_2), .Q(R11), .clk(clk), .clr(in_1));
  Register #(.width(32)) register_21 (.D(W19), .en(in_2), .Q(R19), .clk(clk), .clr(in_1));
  Register #(.width(32)) register_22 (.D(W28), .en(in_2), .Q(R28), .clk(clk), .clr(in_1));
  Register #(.width(32)) register_23 (.D(W5), .en(in_2), .Q(R5), .clk(clk), .clr(in_1));
  Register #(.width(32)) register_24 (.D(W12), .en(in_2), .Q(R12), .clk(clk), .clr(in_1));
  Register #(.width(32)) register_25 (.D(W20), .en(in_2), .Q(R20), .clk(clk), .clr(in_1));
  Register #(.width(32)) register_26 (.D(W29), .en(in_2), .Q(R29), .clk(clk), .clr(in_1));
  Demultiplexer #(.select(5), .width(32), .tristate("true"), .enable("false")) demultiplexer_1 (
    .out1(W1), .out2(W2), .out3(W3), .out4(W4), .out5(W5), .out6(W6), .out7(W7), .out8(W8), .out9(W9),
    .out10(W10), .out11(W11), .out12(W12), .out13(W13), .out14(W14), .out15(W15), .out16(W16), .out17(W17),
    .out18(W18), .out19(W19), .out20(W20), .out21(W21), .out22(W22), .out23(W23), .out24(W24), .out25(W25),
    .out26(W26), .out27(W27), .out28(W28), .out29(W29), .out30(W30), .out31(W31), .in(in_6), .sel(in_5));  // open: out0
  Register #(.width(32)) register_27 (.D(W6), .en(in_2), .Q(R6), .clk(clk), .clr(in_1));
  Register #(.width(32)) register_28 (.D(W13), .en(in_2), .Q(R13), .clk(clk), .clr(in_1));
  Register #(.width(32)) register_29 (.D(W21), .en(in_2), .Q(R21), .clk(clk), .clr(in_1));
  Register #(.width(32)) register_30 (.D(W30), .en(in_2), .Q(R30), .clk(clk), .clr(in_1));
  Register #(.width(32)) register_31 (.D(W22), .en(in_2), .Q(R22), .clk(clk), .clr(in_1));
  Register #(.width(32)) register_32 (.D(W31), .en(in_2), .Q(R31), .clk(clk), .clr(in_1));

  // Other names for the same wires on the sheet: Data[31:0] = in_6; rd[4:0] = in_5; RD2[31:0] = out_8; reset = in_1;
  //   rs[4:0] = in_3; rt[4:0] = in_4; WE = in_2
endmodule

module ALU (
  input  [2:0] in_1,
  input  [31:0] in_2,
  input  [31:0] in_3,
  output [31:0] ALUResult
);

  wire [31:0] adder_1_out, and_1_out, or_1_out, subtractor_1_out;

  assign and_1_out = in_2 & in_3;  // AND_Gate and_1, 32 bits wide
  assign or_1_out = in_2 | in_3;  // OR_Gate or_1, 32 bits wide
  Adder #(.width(32)) adder_1 (.a(in_2), .b(in_3), .out(adder_1_out));  // open: cin, cout
  Subtractor #(.width(32)) subtractor_1 (.a(in_2), .b(in_3), .out(subtractor_1_out));  // open: bin, bout
  Multiplexer #(.select(3), .width(32)) multiplexer_1 (
    .in0(and_1_out), .in1(or_1_out), .in2(adder_1_out), .in3({32{1'b0}}), .in4({32{1'b0}}), .in5({32{1'b0}}),
    .in6(subtractor_1_out), .in7({32{1'b0}}), .out(ALUResult), .sel(in_1));  // open: en

  // Other names for the same wires on the sheet: ALUControl[2:0] = in_1; SourceA[31:0] = in_2; SourceB[31:0] = in_3
endmodule

module DM (
  input  in_1,
  input  in_2,
  input  [31:0] in_3,
  input  [31:0] in_4,
  output [31:0] ReadData
);

  wire clock_1_out;

  Clock clock_1 (.out(clock_1_out));
  RAM #(.addrWidth(5), .dataWidth(32), .bus("separate")) ram_1 (
    .addr(in_3[6:2]), .din(in_4), .data(ReadData), .str(in_2), .clk(clock_1_out), .clr(in_1));  // open: sel, ld

  // Other names for the same wires on the sheet: ALUResult[31:0] = in_3; MemWrite = in_2; reset = in_1;
  //   WriteData[31:0] = in_4
endmodule

module EXT (
  input  [15:0] in_1,
  input  [1:0] in_2,
  output [31:0] ImmExtend
);

  wire [31:0] bit_extender_1_out, bit_extender_2_out, bit_extender_3_out;

  assign bit_extender_1_out = {{16{in_1[15]}}, in_1};  // Bit_Extender bit_extender_1
  assign bit_extender_2_out = {{16{1'b0}}, in_1};  // Bit_Extender bit_extender_2
  assign bit_extender_3_out = {{14{in_1[15]}}, {in_1, 2'b00}};  // Bit_Extender bit_extender_3
  Multiplexer #(.select(2), .width(32)) multiplexer_1 (
    .in0(bit_extender_1_out), .in1(bit_extender_2_out), .in2({in_1, {16{1'b0}}}), .in3(bit_extender_3_out),
    .out(ImmExtend), .sel(in_2));  // open: en

  // Other names for the same wires on the sheet: Imm[15:0] = in_1; EXTControl[1:0] = in_2
endmodule

module Controller (
  input  [5:0] in_1,
  input  [5:0] in_2,
  input  [31:0] in_3,
  output RegDst,
  output RegWrite,
  output MemtoReg,
  output ALUSource,
  output MemWrite,
  output Branch,
  output [1:0] EXTControl,
  output [2:0] ALUControl
);

  wire controller1_1_memwrite, controller1_1_regwrite, nop, not_1_out, not_2_out;

  Comparator #(.width(32), .mode("unsigned")) comparator_1 (.a(in_3), .b({32{1'b0}}), .eq(nop));  // open: gt, lt
  Controller1 controller1_1 (
    .f5(in_2[5]), .f4(in_2[4]), .f3(in_2[3]), .f2(in_2[2]), .f1(in_2[1]), .f0(in_2[0]), .op5(in_1[5]),
    .op4(in_1[4]), .op3(in_1[3]), .op2(in_1[2]), .op1(in_1[1]), .op0(in_1[0]), .RegDst(RegDst),
    .RegWrite(controller1_1_regwrite), .MemtoReg(MemtoReg), .ALUSource(ALUSource),
    .MemWrite(controller1_1_memwrite), .Branch(Branch), .EXTControl(EXTControl), .ALUControl(ALUControl));
  not not_1 (not_1_out, nop);
  not not_2 (not_2_out, nop);
  and and_1 (RegWrite, controller1_1_regwrite, not_1_out);
  and and_2 (MemWrite, not_2_out, controller1_1_memwrite);

  // Other names for the same wires on the sheet: func[5:0] = in_2; Instr[31:0] = in_3; Opcode[5:0] = in_1
endmodule

module NPC (
  input  [31:0] in_1,
  input  [15:0] in_2,
  input  in_3,
  output [31:0] NPC
);

  wire [31:0] adder_1_out, adder_2_out, bit_extender_1_out, shifter_1_out;

  assign bit_extender_1_out = {{16{in_2[15]}}, in_2};  // Bit_Extender bit_extender_1
  Adder #(.width(32)) adder_1 (.a(in_1), .b(32'h4), .out(adder_1_out));  // open: cin, cout
  Shifter #(.width(32)) shifter_1 (.in(bit_extender_1_out), .\dist (5'b00010), .out(shifter_1_out));
  Multiplexer #(.width(32)) multiplexer_1 (.in0(adder_1_out), .in1(adder_2_out), .out(NPC), .sel(in_3));  // open: en
  Adder #(.width(32)) adder_2 (.a(adder_1_out), .b(shifter_1_out), .out(adder_2_out));  // open: cin, cout

  // Other names for the same wires on the sheet: Imm[15:0] = in_2; PC[31:0] = in_1; PCSource = in_3
endmodule

module Controller1 (
  input  f5,
  input  f4,
  input  f3,
  input  f2,
  input  f1,
  input  f0,
  input  op5,
  input  op4,
  input  op3,
  input  op2,
  input  op1,
  input  op0,
  output RegDst,
  output RegWrite,
  output MemtoReg,
  output ALUSource,
  output MemWrite,
  output Branch,
  output [1:0] EXTControl,
  output [2:0] ALUControl
);

  wire add_out, jal_out, lui_out, not_1_out, not_2_out, not_3_out, not_4_out, not_5_out, not_6_out,
       not_7_out, not_8_out, not_9_out, not_10_out, not_11_out, not_12_out, sub_out;

  not not_1 (not_1_out, f5);
  not not_2 (not_2_out, f4);
  not not_3 (not_3_out, f3);
  not not_4 (not_4_out, f2);
  not not_5 (not_5_out, f1);
  not not_6 (not_6_out, f0);
  not not_7 (not_7_out, op5);
  not not_8 (not_8_out, op4);
  not not_9 (not_9_out, op3);
  not not_10 (not_10_out, op2);
  not not_11 (not_11_out, op1);
  not not_12 (not_12_out, op0);
  and add (add_out, not_12_out, not_11_out, not_10_out, not_9_out, not_8_out, not_7_out, not_6_out, not_5_out, not_4_out, not_3_out, not_2_out, f5);
  and sub (sub_out, not_12_out, not_11_out, not_10_out, not_9_out, not_8_out, not_7_out, not_6_out, f1, not_4_out, not_3_out, not_2_out, f5);
  and ori (ALUControl[0], op0, not_11_out, op2, op3, not_8_out, not_7_out);
  and lw (MemtoReg, op0, op1, not_10_out, not_9_out, not_8_out, op5);
  and sw (MemWrite, op0, op1, not_10_out, op3, not_8_out, op5);
  and beq (Branch, not_12_out, not_11_out, op2, not_9_out, not_8_out, not_7_out);
  and lui (lui_out, op0, op1, op2, op3, not_8_out, not_7_out);
  and jal (jal_out, op0, op1, not_10_out, not_9_out, not_8_out, not_7_out);
  // AND_Gate jr has open pins: in0=not_12_out, in1=not_11_out, in2=not_10_out, in3=not_9_out, in4=not_8_out, in5=not_7_out, in6=not_6_out, in7=not_5_out, in8=not_4_out, in9=f3, in10=not_2_out, in11=not_1_out, out=open
  or or_1 (ALUControl[2], sub_out, Branch);
  or or_2 (ALUControl[1], add_out, sub_out, MemtoReg, MemWrite, Branch, lui_out);
  or or_3 (EXTControl[1], Branch, lui_out);
  or or_4 (EXTControl[0], ALUControl[0], Branch);
  or u_regDst (RegDst, add_out, sub_out);
  or u_RegWrite (RegWrite, add_out, sub_out, ALUControl[0], MemtoReg, lui_out, jal_out);
  or u_ALuSource (ALUSource, ALUControl[0], MemtoReg, MemWrite, lui_out);
endmodule

module BranchControl (
  input  [31:0] ALUResult,
  input  Branch,
  output PCSource
);

  wire comparator_1_eq;

  Comparator #(.width(32), .mode("unsigned")) comparator_1 (
    .a({32{1'b0}}), .b(ALUResult), .eq(comparator_1_eq));  // open: gt, lt
  and and_1 (PCSource, comparator_1_eq, Branch);
endmodule
